# Fritzing sketch snake (saved by Fritzing 0.9.2b)
breadboards: 2

parts:
  S1 = Pushbutton [package="[THT]"]
  S2 = Pushbutton [package="[THT]"]
  R1 = Resistor [tolerance=±5% resistance=220 package=THT]
  R2 = Resistor [tolerance=±5% resistance=220 package=THT]
  IC1 = SHIFT REGISTER [part_number=SH74HC595 package=dil16]
  IC2 = SHIFT REGISTER [part_number=SH74HC595 package=dil16]
  パーツ1 = Arduino Yun
  R3 = Resistor [tolerance=±0.5% resistance=220 package=THT]
  Disp1 = LBT2088AH [part_number=OSL641501-BRA]
  R4 = Resistor [tolerance=±5% resistance=220 package=THT]  # not connected
  R5 = Resistor [tolerance=±5% resistance=220 package=THT]  # not connected
  R6 = Resistor [tolerance=±5% resistance=220 package=THT]  # not connected
  R7 = Resistor [tolerance=±5% resistance=220 package=THT]
  R8 = Resistor [tolerance=±5% resistance=220 package=THT]
  R9 = Resistor [tolerance=±5% resistance=220 package=THT]  # not connected
  R10 = Resistor [tolerance=±5% resistance=220 package=THT]  # not connected
  R11 = Resistor [tolerance=±5% resistance=220 package=THT]  # not connected
  R12 = Resistor [tolerance=±5% resistance=220 package=THT]  # not connected
  R13 = Resistor [tolerance=±5% resistance=220 package=THT]
  R14 = Resistor [tolerance=±5% resistance=220 package=THT]
  R15 = Resistor [tolerance=±5% resistance=220 package=THT]
  R16 = Resistor [tolerance=±5% resistance=220 package=THT]  # not connected
  R17 = Resistor [tolerance=±5% resistance=220 package=THT]
  R18 = Resistor [tolerance=±5% resistance=220 package=THT]

nets:
  N1: S1.Pin_1, S1.Pin_2, R2.Pin_0, パーツ1.D5_PWM
  VCC: S1.Pin_3, S1.Pin_4, S2.Pin_3, S2.Pin_4, IC1.SCL, IC1.VCC, IC2.SCL, IC2.VCC, パーツ1.5V
  N2: S2.Pin_1, S2.Pin_2, R1.Pin_0, パーツ1.D6_PWM
  GND: R1.Pin_1, R2.Pin_1, IC1.GND, IC1.G, IC2.GND, IC2.G, パーツ1.GND
  N3: IC1.QB, R18.Pin_0
  N4: IC1.QC, R14.Pin_1
  N5: IC1.QD, R17.Pin_0
  N6: IC1.QE, R3.Pin_1
  N7: IC1.QF, R13.Pin_1
  N8: IC1.QG, R7.Pin_1
  N9: IC1.QH, R8.Pin_1
  N10: IC1.QH*, IC2.SER
  N11: IC1.SCK, IC2.SCK, パーツ1.D12/MISO
  N12: IC1.RCK, IC2.RCK, パーツ1.D8
  N13: IC1.SER, パーツ1.D11_PWM/MOSI
  N14: IC1.QA, R15.Pin_0
  N15: IC2.QB, Disp1.pin_3
  N16: IC2.QC, Disp1.pin_4
  N17: IC2.QD, Disp1.pin_10
  N18: IC2.QE, Disp1.pin_6
  N19: IC2.QF, Disp1.pin_11
  N20: IC2.QG, Disp1.pin_15
  N21: IC2.QH, Disp1.pin_16
  N22: IC2.QA, Disp1.pin_13
  N23: R3.Pin_0, Disp1.pin1
  N24: Disp1.pin2, R7.Pin_0
  N25: Disp1.pin_5, R8.Pin_0
  N26: Disp1.pin_7, R13.Pin_0
  N27: Disp1.pin_8, R14.Pin_0
  N28: Disp1.pin_9, R15.Pin_1
  N29: Disp1.pin_12, R17.Pin_1
  N30: Disp1.pin_14, R18.Pin_1
